# Fritzing sketch sketch (saved by Fritzing 0.9.5d)
# 18650 Li-ion Battery: CC-BY Dr Kristofer Chan, King's College London/Remote-research.org
breadboards: 1

parts:
  U1 = LuaNode32 / ESP32 [part_number=ESP32S-PIN30]
  Part1 = Motor Driver 1A Dual TB6612FNG  # not connected
  14500/500mAh_3_7V_Li-ion = 18650 Li-ion Battery [package=battery-18650]
  VCC1 = Battery block 9V
  rear_motor = DC Motor  # not connected
  front_motor = DC Motor  # not connected

nets:
  N1: U1.GND, 14500/500mAh_3_7V_Li-ion.-, VCC1.-
  N2: U1.Vin, 14500/500mAh_3_7V_Li-ion.+

custom parts:
  LuaNode32 / ESP32: New Image for LuaNode32 DOIT ESP32 DEVKIT V1. Base parts from LuaNode32 / ESP32 ESP32 based LuaNode32 by G.Noorlander DOIT Esp32 DevKit v1 (30 pins long, 11 pins width) by Werner Rothschopf (modified by vanepp Dec 2018)
  18650 Li-ion Battery: 18650 li-ion Battery Standard 18650 battery with interactive connectors Creative Common Attribution 4.0 International (CC-BY 4.0) license. Any use of this part requires attribution of Dr Kristofer Chan, Department of Geography, King's College London. Contact kristofer.chan [at] kcl.ac.uk OR kris [at] remote-research.org for further information.
